// Logisim project calculadora-5bits-funcional.circ as structural Verilog: 3 circuits, main circuit main
module main (
  input  A0,
  input  A1,
  input  A2,
  input  A3,
  input  A4,
  input  B0,
  input  B1,
  input  B2,
  input  B3,
  input  B4,
  input  in_11,
  output S0,
  output S1,
  output S2,
  output S3,
  output S4
);

  wire full_adder_1_cout, full_adder_2_cout, full_adder_3_cout, full_adder_4_cout;

  Full_Adder full_adder_1 (.A(A0), .B(B0), .Cout(full_adder_1_cout), .Cin(in_11), .Soma(S0));
  Full_Adder full_adder_2 (.A(A1), .B(B1), .Cout(full_adder_2_cout), .Cin(full_adder_1_cout), .Soma(S1));
  Full_Adder full_adder_3 (.A(A2), .B(B2), .Cout(full_adder_3_cout), .Cin(full_adder_2_cout), .Soma(S2));
  Full_Adder full_adder_4 (.A(A3), .B(B3), .Cout(full_adder_4_cout), .Cin(full_adder_3_cout), .Soma(S3));
  Full_Adder full_adder_5 (.A(A4), .B(B4), .Cout(S4), .Cin(full_adder_4_cout));  // open: Soma
endmodule

module Half_Adder (
  input  A,
  input  B,
  output out_3,
  output out_4
);

  xor Soma (out_3, A, B);
  and Carry (out_4, B, A);
endmodule

module Full_Adder (
  input  A,
  input  B,
  input  Cin,
  output Soma,
  output Cout
);

  wire half_adder_1_out_3, half_adder_1_out_4, half_adder_2_out_4;

  Half_Adder half_adder_1 (.A(A), .B(B), .out_3(half_adder_1_out_3), .out_4(half_adder_1_out_4));
  Half_Adder half_adder_2 (.A(half_adder_1_out_3), .B(Cin), .out_3(Soma), .out_4(half_adder_2_out_4));
  or u_Cout (Cout, half_adder_1_out_4, half_adder_2_out_4);
endmodule
