// Logisim project full-adder.circ as structural Verilog: 2 circuits, main circuit main
module main (
  input  A,
  input  B,
  input  Cin,
  output Soma,
  output Cout
);

  wire half_adder_1_out_3, half_adder_1_out_4, half_adder_2_out_4;

  Half_Adder half_adder_1 (.A(A), .B(B), .out_3(half_adder_1_out_3), .out_4(half_adder_1_out_4));
  Half_Adder half_adder_2 (.A(half_adder_1_out_3), .B(Cin), .out_3(Soma), .out_4(half_adder_2_out_4));
  or u_Cout (Cout, half_adder_1_out_4, half_adder_2_out_4);
endmodule

module Half_Adder (
  input  A,
  input  B,
  output out_3,
  output out_4
);

  xor Soma (out_3, A, B);
  and Carry (out_4, B, A);
endmodule
