// Logisim project half-adder.circ as structural Verilog: 2 circuits, main circuit main
module main (
  input  A,
  input  B
);

  wire Carry_out, Soma_out;

  xor Soma (Soma_out, A, B);
  and Carry (Carry_out, B, A);
  Half_Adder half_adder_1 ();  // open: A, B
endmodule

module Half_Adder (
  input  A,
  input  B
);

  wire Carry_out, Soma_out;

  xor Soma (Soma_out, A, B);
  and Carry (Carry_out, B, A);
endmodule
